# Fritzing sketch Fritzing-BinaryClock (saved by Fritzing 0.8.5b)
breadboards: 1

parts:
  U3 = 74HC595 [part_number=Columns package="DIP16 [THT]"]
  U2 = 74HC595 [part_number=Rows package="DIP16 [THT]"]
  IC1 = ULN2803A [package=THT]
  8x8_LED_Matrix1 = Led Matrix LD1088-BS
  R1 = Resistor [tolerance=±5% resistance=260 package=THT]
  R2 = Resistor [tolerance=±5% resistance=260 package=THT]
  R3 = Resistor [tolerance=±5% resistance=260 package=THT]
  R4 = Resistor [tolerance=±5% resistance=260 package=THT]
  R5 = Resistor [tolerance=±5% resistance=260 package=THT]
  R6 = Resistor [tolerance=±5% resistance=260 package=THT]
  R7 = Resistor [tolerance=±5% resistance=260 package=THT]
  R8 = Resistor [tolerance=±5% resistance=260 package=THT]
  V1 = DC Power [voltage=5V part_number="3 AA batteries"]
  C1 = Capacitor [part_number=100n package=cap-pth-small2]
  R9 = Resistor [tolerance=±5% resistance=10k package=THT]
  C2 = Capacitor [part_number=100n package=cap-pth-small2]
  FTDI_header = FTDI_BASIC [package=ftdi_basic]
  U1 = atmega328 [package=dip]
  XTAL1 = Crystal [frequency="16 Mhz" package=THT]
  C3 = Capacitor [part_number=22p package=cap-pth-small2]
  C4 = Capacitor [part_number=22p package=cap-pth-small2]
  S1 = Pushbutton [package="[THT]"]
  S2 = Pushbutton [package="[THT]"]
  S3 = Pushbutton [package="[THT]"]
  S4 = Pushbutton [package="[THT]"]

nets:
  N1: U3.Q1, IC1.In_2
  N2: U3.Q2, IC1.In_3
  N3: U3.Q3, IC1.In_4
  N4: U3.Q4, IC1.In_5
  N5: U3.Q5, IC1.In_6
  N6: U3.Q6, IC1.In_7
  N7: U3.Q7, IC1.In_8
  GND: U3.GND, U3.OE, U2.GND, U2.OE, IC1.0V, V1.V-, C1.1, FTDI_header.1, U1.GND, C3.2, C4.1
  N8: U3.Q7', U2.DS
  VCC: U3.MR, U3.VCC, U2.MR, U2.VCC, V1.V+, C1.2, R9.Pin_1, FTDI_header.3, U1.VCC, U1.AVCC, S1.Pin_3, S2.Pin_3, S3.Pin_3, S4.Pin_3, S4.Pin_4
  N9: U3.SH_CP, U2.SH_CP, U1.D12
  N10: U3.ST_CP, U2.ST_CP, U1.D8
  N11: U3.DS, U1.D11_(PWM)
  N12: U3.Q0, IC1.In_1
  N13: U2.Q1, R2.Pin_1
  N14: U2.Q2, R3.Pin_1
  N15: U2.Q3, R4.Pin_1
  N16: U2.Q4, R5.Pin_1
  N17: U2.Q5, R6.Pin_1
  N18: U2.Q6, R7.Pin_1
  N19: U2.Q7, R8.Pin_1
  N20: U2.Q0, R1.Pin_1
  N21: IC1.Out_8, 8x8_LED_Matrix1.Pin_16
  N22: IC1.Out_7, 8x8_LED_Matrix1.Pin_15
  N23: IC1.Out_6, 8x8_LED_Matrix1.Pin_11
  N24: IC1.Out_5, 8x8_LED_Matrix1.Pin_6
  N25: IC1.Out_4, 8x8_LED_Matrix1.Pin_10
  N26: IC1.Out_3, 8x8_LED_Matrix1.Pin_4
  N27: IC1.Out_2, 8x8_LED_Matrix1.Pin_3
  N28: IC1.Out_1, 8x8_LED_Matrix1.Pin_13
  N29: 8x8_LED_Matrix1.Pin_1, R5.Pin_0
  N30: 8x8_LED_Matrix1.Pin_2, R7.Pin_0
  N31: 8x8_LED_Matrix1.Pin_5, R8.Pin_0
  N32: 8x8_LED_Matrix1.Pin_7, R6.Pin_0
  N33: 8x8_LED_Matrix1.Pin_8, R3.Pin_0
  N34: 8x8_LED_Matrix1.Pin_9, R1.Pin_0
  N35: 8x8_LED_Matrix1.Pin_12, R4.Pin_0
  N36: 8x8_LED_Matrix1.Pin14, R2.Pin_0
  N37: R9.Pin_0, C2.1, U1.RESET
  N38: C2.2, FTDI_header.6
  N39: FTDI_header.5, U1.D1_(TX)
  N40: FTDI_header.4, U1.D0_(RX)
  N41: U1.D2, S1.Pin_1, S1.Pin_2
  N42: U1.D3_(PWM), S2.Pin_1, S2.Pin_2
  N43: U1.D4, S3.Pin_2
  N44: U1.XLAT1, XTAL1.pin_0, C3.1
  N45: U1.XLAT2, XTAL1.pin_1, C4.2
  N46: U1.D5_(PWM), S4.Pin_2

custom parts:
  Led Matrix LD1088-BS: Red Color Common cathode 8x8 LED Matrix
  FTDI_BASIC: FTDI Basic header with labels
